# Fritzing sketch scheme (saved by Fritzing 0.9.4)
breadboards: 1

parts:
  WeMos_D1_Mini_Micro_SD_Shield1 = WeMos D1 Mini Micro SD Shield
  BAT1 = 12 battery [package=battery]
  Stäng = Pushbutton [package="[THT]"]
  Öppna = Pushbutton [package="[THT]"]
  U1 = 2-Channel 5v Relay Shield [package=relay-2ch5v10a]
  Hissmotor_alt_linjärmotor = DC Motor

nets:
  5V: WeMos_D1_Mini_Micro_SD_Shield1.5V, WeMos_D1_Mini_Micro_SD_Shield1.D7, U1.VCC, U1.IN2
  N1: WeMos_D1_Mini_Micro_SD_Shield1.D2, Stäng.Pin_1, Stäng.Pin_2
  N2: WeMos_D1_Mini_Micro_SD_Shield1.D3, Öppna.Pin_1, Öppna.Pin_2
  N3: WeMos_D1_Mini_Micro_SD_Shield1.D6, U1.IN1
  N4: WeMos_D1_Mini_Micro_SD_Shield1.G, Stäng.Pin_3, Stäng.Pin_4, Öppna.Pin_3, Öppna.Pin_4, U1.GND
  N5: BAT1.-, U1.K1-On, U1.K2-On
  N6: BAT1.+, U1.K1-Off, U1.K2-Off
  N7: U1.K1-In, Hissmotor_alt_linjärmotor.pin_1
  N8: U1.K2-In, Hissmotor_alt_linjärmotor.pin_2

custom parts:
  12 battery: 12V lead acid type battery, like the Husqvarna YTH2448 12V 35AH battery. This is the mini version 1/4 the size of the actual battery to be closer to typical breadboard parts (around 2in wide rathher than 7in). The pads in pcb are sized to accomidate up to 14ga wire (as these batterys will deliver high currents.)
  2-Channel 5v Relay Shield: 2 Channel 5v Relay Shield w. 2x SPD-06VDC-SD-C
